# Fritzing sketch fritzing (saved by Fritzing 0.9.3b)

parts:
  Nano1 = Arduino Nano v2.3
  U1 = TRANSCHIPTC5747 [package=camera_sfv24r-2st_2]

nets:
  N1: Nano1.D1TX, U1.AGND
  N2: Nano1.D0RX, U1.SCLK
  N3: Nano1.GND, U1.DOUT_6
  N4: Nano1.D2, U1.LED_CTRL
  N5: Nano1.D3, U1.SHIELD
  N6: Nano1.D4, U1.PS2
  N7: Nano1.D5, U1.PS1
  N8: Nano1.D6, U1.CLK_IN
  N9: Nano1.D7, U1.DGND
  N10: Nano1.D8, U1.VCLK_OUT
  N11: Nano1.D9, U1.VALIDH
  N12: Nano1.D10, U1.VALIDV
  N13: Nano1.D12, U1.SDIN
  N14: Nano1.3V3, U1.DOUT_5
  N15: Nano1.A5, U1.DOUT_1
  N16: Nano1.A4, U1.DOUT_0
